# Fritzing sketch schematicdesign (saved by Fritzing 0.9.2b)
breadboards: 1

parts:
  Part1 = Arduino Uno (Rev3)
  LED1 = LED - 5mm [color="Red (633nm)" package="5 mm [THT]"]
  R1 = Resistor [tolerance=±5% resistance=220 package=THT]
  R2 = Resistor [tolerance=±5% resistance=220 package=THT]
  R3 = Resistor [tolerance=±5% resistance=220 package=THT]
  LED2 = LED - 5mm [color="Red (633nm)" package="5 mm [THT]"]
  LED3 = LED - 5mm [color="Red (633nm)" package="5 mm [THT]"]

nets:
  N1: Part1.D2, LED1.cathode
  N2: Part1.D3_PWM, LED3.cathode
  N3: Part1.D4, LED2.cathode
  N4: Part1.GND, R1.Pin_0, R2.Pin_0, R3.Pin_0
  N5: LED1.anode, R1.Pin_1
  N6: R2.Pin_1, LED3.anode
  N7: R3.Pin_1, LED2.anode
