# Fritzing sketch schematicpowerbutton (saved by Fritzing 0.9.2b)
breadboards: 1

parts:
  Part1 = Arduino Uno (Rev3)
  LED1 = LED - 5mm [color="Red (633nm)" package="5 mm [THT]"]
  LED2 = LED - 5mm [color="Red (633nm)" package="5 mm [THT]"]
  LED3 = LED - 5mm [color="Red (633nm)" package="5 mm [THT]"]
  R1 = Resistor [tolerance=±5% resistance=220 package=THT]
  R2 = Resistor [tolerance=±5% resistance=220 package=THT]
  R3 = Resistor [tolerance=±5% resistance=220 package=THT]
  S1 = Pushbutton [package="[THT]"]
  R4 = Resistor [tolerance=±5% resistance=220 package=THT]

nets:
  N1: Part1.D2, LED1.anode
  N2: Part1.D3_PWM, LED2.anode
  N3: Part1.D4, LED3.anode
  N4: Part1.D5_PWM, S1.Pin_1, S1.Pin_2, R4.Pin_0
  N5: Part1.5V, S1.Pin_3, S1.Pin_4
  N6: LED1.cathode, R1.Pin_0
  N7: LED2.cathode, R2.Pin_0
  N8: LED3.cathode, R3.Pin_0
  N9: R1.Pin_1, R2.Pin_1, R3.Pin_1, R4.Pin_1
